// Logisim project CPU(S-MIPS).circ as structural Verilog: 1 circuit, main circuit S-MIPS
module S_MIPS (
  input  [31:0] RAM_Out_0,
  input  [31:0] RAM_Out_1,
  input  [31:0] RAM_Out_2,
  input  [31:0] RAM_Out_3,
  input  [3:0] Read_Time,
  input  [3:0] Write_Time,
  input  Reset,
  input  Clock,
  input  Kbd_Available,
  input  [6:0] Kbd_ASCII_Data,
  output [31:0] RAM_In_0,
  output [31:0] RAM_In_1,
  output [31:0] RAM_In_2,
  output [31:0] RAM_In_3,
  output Halt,
  output [15:0] Address,
  output Kbd_Enable,
  output Kbd_Clear,
  output TTY_Enable,
  output [6:0] TTY_ASCII_Data,
  output [3:0] Mask,
  output nRead_Write,
  output Chip_Select
);

  wire en_MC, fetch, fetched, inst_R_W, rst, Start, upd;
  wire [3:0] mask_t;
  wire [15:0] inst_addrs;
  wire [31:0] inp_Word, inst, Out_Word, PC;

  InstructionMemory instructionmemory_1 (
    .PC_ProgramCounter(PC), .fetch(fetch), .Word(Out_Word), .upd_InstructionUpdated(upd), .rst_reset(rst),
    .addrs(inst_addrs), .mask(mask_t), .R_W(inst_R_W), .Chip_Select(en_MC), .Instruction(inst),
    .fetched(fetched));
  Control_Unit control_unit_1 (
    .START(Start), .FETCHED(fetched), .HALT(Halt), .RESET(Reset), .fetch(fetch), .reset_2(rst));  // open: EXECUTED
  Memory_Controller memory_controller_1 (
    .Address(inst_addrs), .Input_Word(inp_Word), .Mask(mask_t), .O0(RAM_Out_0), .O1(RAM_Out_1),
    .O2(RAM_Out_2), .O3(RAM_Out_3), .R_W(inst_R_W), .Chip_Select(en_MC), .Read_Time(Read_Time),
    .Write_Time(Write_Time), .Address_2(Address), .OW_Out_Word(Out_Word), .Mask_2(Mask), .R_W_2(nRead_Write),
    .CS(Chip_Select), .Updated(upd));  // open: I0, I1, I2, I3
  // DataPath datapath_1: pin names not known; wires that end beside it: Kbd_ASCII_Data, Kbd_Available, inst, fetch, rst, PC, TTY_Enable, TTY_ASCII_Data, fetched, Halt

  // Other names for the same wires on the sheet: CLK = Clock; CLR = Reset; CS = Chip_Select;
  //   KBD_AVAIL = Kbd_Available; KBD_CLR = Kbd_Clear; KBD_DATA[6:0] = Kbd_ASCII_Data; RAM_A[15:0] = Address;
  //   RAM_INPUT_0[31:0] = RAM_In_0; RAM_INPUT_1[31:0] = RAM_In_1; RAM_INPUT_2[31:0] = RAM_In_2;
  //   RAM_INPUT_3[31:0] = RAM_In_3; RAM_MASK[3:0] = Mask; RO0[31:0] = RAM_Out_0; RO1[31:0] = RAM_Out_1;
  //   RO2[31:0] = RAM_Out_2; RO3[31:0] = RAM_Out_3; RW = nRead_Write; STOP = Halt; TTY_DATA[6:0] = TTY_ASCII_Data

  // Notes on the sheet:
  //   RAM TIMING
  //   KEYBOARD
  //   DATA FROM RAM
  //   RAM ADDRESS
  //   KEYBOARD
  //   TTY
  //   DATA WRITE MASK
  //   RAM CONTROL
  //   DATA TO RAM
endmodule
