// Logisim project Control_Unit.circ as structural Verilog: 1 circuit, main circuit Control Unit
module Control_Unit (
  input  [5:0] FuncCode,
  input  [5:0] OpCode,
  input  START,
  input  FETCHED,
  input  RESET,
  output [17:0] SelectorCodes,
  output [2:0] FC_Selector,
  output [3:0] ALU_Op,
  output fetch,
  output reset_2,
  output rnd_kbd_Selector,
  output TTY_Enable,
  output ReadInstruction,
  output ChipSelect,
  output R_W
);

  wire clk, demultiplexer_1_out0, demultiplexer_2_out0, demultiplexer_3_out0, demultiplexer_4_out0,
       demultiplexer_5_out0, demultiplexer_6_out0, FETCH_q, halt, IDLE_q, Load, Main,
       MandarAqui_El_Segundo_SelectorCodes,
       MandarAqui_las_senales_que_no_son_de_la_DP_para_escribir_en_la_ram_con_la_info_del_datapath, or_1_out,
       or_3_out, or_4_out, or_5_out, or_6_out, Pop, Push, ReadMemory_2_q, ReadMemory_q, Store, undriven,
       WriteMemory_2_q;

  or or_1 (or_1_out, demultiplexer_1_out0, 1'b1);
  D_Flip_Flop IDLE (.clk(or_1_out), .D(clk), .Q(IDLE_q), .preset(1'b1));  // open: Qn, en, reset
  Demultiplexer #(.enable("false")) demultiplexer_1 (
    .out0(demultiplexer_1_out0), .out1(fetch), .in(IDLE_q), .sel(START));
  Clock clock_1 (.out(clk));
  or or_2 (MandarAqui_las_senales_que_no_son_de_la_DP_para_escribir_en_la_ram_con_la_info_del_datapath, demultiplexer_5_out0, Store);
  or or_3 (or_3_out, demultiplexer_6_out0, undriven, fetch);
  or or_4 (or_4_out, demultiplexer_2_out0, Pop);
  D_Flip_Flop ReadMemory (.clk(or_4_out), .D(clk), .Q(ReadMemory_q));  // open: Qn, preset, en, reset
  D_Flip_Flop WriteMemory (
    .clk(or_5_out), .D(clk), .Q(MandarAqui_El_Segundo_SelectorCodes));  // open: Qn, preset, en, reset
  or or_5 (or_5_out, demultiplexer_3_out0, Push);
  or or_6 (or_6_out, demultiplexer_4_out0, Load);
  D_Flip_Flop ReadMemory_2 (.clk(or_6_out), .D(clk), .Q(ReadMemory_2_q));  // open: Qn, preset, en, reset
  D_Flip_Flop WriteMemory_2 (
    .clk(MandarAqui_las_senales_que_no_son_de_la_DP_para_escribir_en_la_ram_con_la_info_del_datapath),
    .D(clk), .Q(WriteMemory_2_q));  // open: Qn, preset, en, reset
  D_Flip_Flop u_FETCH (.clk(or_3_out), .D(clk), .Q(FETCH_q), .preset(1'b1));  // open: Qn, en, reset
  Demultiplexer #(.enable("false")) demultiplexer_2 (
    .out0(demultiplexer_2_out0), .out1(MandarAqui_El_Segundo_SelectorCodes), .in(ReadMemory_q), .sel(FETCHED));
  Demultiplexer #(.enable("false")) demultiplexer_3 (
    .out0(demultiplexer_3_out0), .out1(MandarAqui_El_Segundo_SelectorCodes),
    .in(MandarAqui_El_Segundo_SelectorCodes), .sel(FETCHED));
  Demultiplexer #(.enable("false")) demultiplexer_4 (
    .out0(demultiplexer_4_out0), .out1(MandarAqui_El_Segundo_SelectorCodes), .in(ReadMemory_2_q),
    .sel(FETCHED));
  Demultiplexer #(.enable("false")) demultiplexer_5 (
    .out0(demultiplexer_5_out0), .out1(MandarAqui_El_Segundo_SelectorCodes), .in(WriteMemory_2_q),
    .sel(FETCHED));
  Demultiplexer #(.enable("false")) demultiplexer_6 (
    .out0(demultiplexer_6_out0), .out1(ReadInstruction), .in(FETCH_q), .sel(FETCHED));
  Switcher_CU switcher_cu_1 (
    .kbd_rnd(rnd_kbd_Selector), .FuncCode(FuncCode), .OpCode(OpCode), .ALU_OP(ALU_Op),
    .TTY_Enable(TTY_Enable), .halt(halt), .SelectorCodes(SelectorCodes), .S_FC(FC_Selector), .pop(Pop),
    .push(Push), .load(Load), .store(Store), .Main_In(ReadInstruction), .Main_Out(Main));

  assign ChipSelect = 1'b1;
  assign R_W = 1'b1;
  assign reset_2 = RESET;

  // Other names for the same wires on the sheet: ReadIns = ReadInstruction;
  //   Return = MandarAqui_El_Segundo_SelectorCodes; rst = RESET; Selector_Codes[17:0] = SelectorCodes

  // Notes on the sheet:
  //   Input_Output_Region
  //   Instruction-Lines
endmodule
