// Logisim project DataPath.circ as structural Verilog: 1 circuit, main circuit DataPath
module DataPath (
  input  KBD_Enable,
  input  [6:0] KBD_Data,
  input  fetch,
  input  reset,
  output TTY_Enable,
  output [6:0] TTY_Data,
  output fetched,
  output halt
);

  wire B_Cero, comparator_1_eq, EI, FC, Jmp, Load, mf_Hi_Lo, R_Hi_Lo, R_W, Store, Upd_Hi, UpdateHi,
       W_SOU_Data;
  wire [1:0] Esp_Ins_S;
  wire [3:0] Op;
  wire [4:0] DA, SA, SB;
  wire [15:0] Const;
  wire [25:0] dest;
  wire [31:0] A, AI, B, B_prime, DATA_HI, DATA_HI_LO, DATA_IN, DATA_INPUT, DATA_LO, Ins, JS,
       multiplexer_2_out, NI, PC, SOU_Data;

  ProgramCounter programcounter_1 (.jmp_addr(NI), .jmp_Jump(Jmp), .rst_Reset(fetch), .Q(PC), .fetch(reset));
  Branch_Control branch_control_1 (
    .JS_Jump_Size(JS), .IA_InstructionAddress(AI), .jmp(Jmp), .FC(FC), .NIR_NextInstructionAddrs(NI));
  assign JS = {{16{1'b0}}, Const};  // Bit_Extender bit_extender_1
  InstructionDecoder instructiondecoder_1 (
    .Instruction(Ins), .DA_DataAddress(DA), .R_W_ReadWrite(R_W), .SA_SelectorA(SA), .SB_SelectorB(SB),
    .Jmp(Jmp), .FC_FlagCondition(FC), .dest(dest), .A(Const), .Op(Op), .Load(Load), .Store(Store),
    .Active_EI(EI), .EspecialInstruction(Esp_Ins_S), .Read_Hi_Lo(R_Hi_Lo), .mf_Hi_Lo(mf_Hi_Lo));  // open: Op_Type
  Multiplexer #(.width(32), .enable("false")) multiplexer_1 (.in0(B), .in1(JS), .out(B_prime), .sel(comparator_1_eq));
  Comparator #(.width(32), .mode("unsigned")) comparator_1 (
    .a(B), .b({32{1'b0}}), .eq(comparator_1_eq));  // open: gt, lt
  Special_Op_Unit special_op_unit_1 (
    .Enable(EI), .EspIns_Selector(Esp_Ins_S), .RS_Data(A), .KBD_Data(KBD_Data), .KBD_Enable(KBD_Enable),
    .Halt(halt), .TTY_DATA(TTY_Data), .TTY_Enable(TTY_Enable), .Write_Data(W_SOU_Data), .RD_Data(SOU_Data));
  Multiplexer #(.width(32), .enable("false")) multiplexer_2 (
    .in0(DATA_IN), .in1(DATA_HI_LO), .out(multiplexer_2_out), .sel(mf_Hi_Lo));
  RegisterFile registerfile_1 (
    .DA_DestinationAddress(DA), .DI_DataInput(DATA_INPUT), .RW_Read_Write(R_W), .Rst_Reset(reset), .SA(SA),
    .SB(SB), .Out_A(A), .Out_B(B));
  Multiplexer #(.width(32), .enable("false")) multiplexer_3 (
    .in0(multiplexer_2_out), .in1(SOU_Data), .out(DATA_INPUT), .sel(W_SOU_Data));
  ALU alu_1 (
    .A(A), .B(B_prime), .Op(Op), .HI_CONTENT(DATA_HI), .UPDATE_HI_LO(Upd_Hi), .Output(DATA_IN),
    .LO_CONTENT(DATA_LO), .B_ZERO(B_Cero));  // open: A___B_unsigned, A___B_signed, A____B, A____B_2, A___B_s
  Hi_Lo_registers_Finished__main main_1 (
    .HI_Content(DATA_HI), .Lo_Content(DATA_LO), .Update(UpdateHi), .Reset(reset), .Read_HI_Lo(R_Hi_Lo),
    .HI_Lo_Data(DATA_HI_LO));

  // Other names for the same wires on the sheet: KBD_En = KBD_Enable; rst = reset; TTY_En = TTY_Enable

  // Notes on the sheet:
  //   Esto se puede mejorar con un soplo multiplexor pero falta todavia un posible data input de hacer save word cuando tengamos MemoryMan vemos aca que hacemos
endmodule
